// Logisim project Controller.circ as structural Verilog: 8 circuits, main circuit Controller
module Controller (
  input  [15:0] Inst,
  input  [3:0] Flags,
  input  Clk,
  input  Reset,
  output Carry,
  output DP_Shift,
  output Imm32_Enable,
  output [4:0] Imm5,
  output [31:0] Imm32,
  output [3:0] ALU_Opcode,
  output [2:0] Rm,
  output [2:0] Rn,
  output [2:0] Rd,
  output [31:0] RAM_Addr,
  output Load,
  output Store,
  output [7:0] PC
);

  wire Conditional_1_verified, Load_Store_1_pc_hold, not_1_out, Opcode_Decoder_1_conditional,
       Opcode_Decoder_1_data_processing, Opcode_Decoder_1_load_store, Opcode_Decoder_1_shift,
       Opcode_Decoder_1_sp_address, Shift_Add_Sub_Mov_1_carry, SP_Address_1_write_enable;
  wire [2:0] Data_Processing_1_rd, Data_Processing_1_rm, Data_Processing_1_rn, Load_Store_1_rd,
       Load_Store_1_rm, Shift_Add_Sub_Mov_1_rd, Shift_Add_Sub_Mov_1_rm, Shift_Add_Sub_Mov_1_rn;
  wire [3:0] Data_Processing_1_alu_opcode, Data_Processing_1_flags_update_mask, flags_apsr_1_flags_out,
       or_1_out, Shift_Add_Sub_Mov_1_alu_opcode, Shift_Add_Sub_Mov_1_flags_update_mask;
  wire [7:0] adder_1_out, adder_2_out, Conditional_1_offset;
  wire [31:0] SP_Address_1_new_stack_pointer, Stack_Pointer_q;

  Register #(.width(32)) Stack_Pointer (
    .D(SP_Address_1_new_stack_pointer), .en(SP_Address_1_write_enable), .clk(Clk), .Q(Stack_Pointer_q),
    .clr(Reset));
  Opcode_Decoder Opcode_Decoder_1 (
    .Opcode(Inst[15:10]), .Data_Processing(Opcode_Decoder_1_data_processing),
    .SP_Address(Opcode_Decoder_1_sp_address), .Load_Store(Opcode_Decoder_1_load_store),
    .Conditional(Opcode_Decoder_1_conditional), .Shift(Opcode_Decoder_1_shift));
  assign or_1_out = Data_Processing_1_flags_update_mask | Shift_Add_Sub_Mov_1_flags_update_mask;  // OR_Gate or_1, 4 bits wide
  Shift_Add_Sub_Mov Shift_Add_Sub_Mov_1 (
    .Imm32_Enable(Imm32_Enable), .Instruction(Inst), .ALU_Opcode(Shift_Add_Sub_Mov_1_alu_opcode),
    .Enable(Opcode_Decoder_1_data_processing), .Carry(Shift_Add_Sub_Mov_1_carry),
    .Flags_Update_Mask(Shift_Add_Sub_Mov_1_flags_update_mask), .Rd(Shift_Add_Sub_Mov_1_rd),
    .Rn(Shift_Add_Sub_Mov_1_rn), .Rm(Shift_Add_Sub_Mov_1_rm), .Imm5(Imm5), .Imm32(Imm32));
  Data_Processing Data_Processing_1 (
    .Instruction(Inst), .ALU_Opcode(Data_Processing_1_alu_opcode), .Enable(Opcode_Decoder_1_sp_address),
    .Rm(Data_Processing_1_rm), .Rn(Data_Processing_1_rn), .Rd(Data_Processing_1_rd),
    .Flags_Update_Mask(Data_Processing_1_flags_update_mask));
  Flags_APSR flags_apsr_1 (
    .Flags_In(or_1_out), .Update_Mask(Flags), .Clk(Clk), .Rst(Reset), .Flags_Out(flags_apsr_1_flags_out));
  Load_Store Load_Store_1 (
    .Instruction(Inst), .Load(Load), .RAM_Addr(RAM_Addr), .Store(Store), .Stack_Pointer(Stack_Pointer_q),
    .Enable(Opcode_Decoder_1_load_store), .Rd(Load_Store_1_rd), .Rm(Load_Store_1_rm), .Clk(Clk),
    .Reset(Reset), .PC_Hold(Load_Store_1_pc_hold));
  Conditional Conditional_1 (
    .Instruction(Inst), .Verified(Conditional_1_verified), .Enable(Opcode_Decoder_1_shift),
    .Offset(Conditional_1_offset), .Z(flags_apsr_1_flags_out[2]), .V(flags_apsr_1_flags_out[0]),
    .N(flags_apsr_1_flags_out[3]), .C(flags_apsr_1_flags_out[1]));
  SP_Address SP_Address_1 (
    .New_Stack_Pointer(SP_Address_1_new_stack_pointer), .Stack_Pointer(Stack_Pointer_q),
    .Enable(Opcode_Decoder_1_conditional), .Instruction(Inst), .Write_Enable(SP_Address_1_write_enable));
  Adder adder_1 (.a(8'h3), .b(Conditional_1_offset), .out(adder_1_out), .cin(1'b0));  // open: cout
  Adder adder_2 (.a(adder_1_out), .b(PC), .out(adder_2_out), .cin(1'b0));  // open: cout
  and and_1 (DP_Shift, Opcode_Decoder_1_data_processing, ~Opcode_Decoder_1_sp_address);  // AND_Gate
  not not_1 (not_1_out, Load_Store_1_pc_hold);
  Counter counter_1 (
    .clr(Reset), .load(Conditional_1_verified), .up(1'b1), .count(not_1_out), .clk(Clk), .D(adder_2_out),
    .Q(PC));  // open: carry
  Multiplexer #(.enable("false")) multiplexer_1 (
    .in0(flags_apsr_1_flags_out[1]), .in1(Shift_Add_Sub_Mov_1_carry), .out(Carry), .sel(DP_Shift));
  assign ALU_Opcode = Shift_Add_Sub_Mov_1_alu_opcode | Data_Processing_1_alu_opcode;  // OR_Gate or_2, 4 bits wide
  assign Rm = Shift_Add_Sub_Mov_1_rm | Data_Processing_1_rm | Load_Store_1_rm;  // OR_Gate or_3, 3 bits wide
  assign Rn = Shift_Add_Sub_Mov_1_rn | Data_Processing_1_rn;  // OR_Gate or_4, 3 bits wide
  assign Rd = Shift_Add_Sub_Mov_1_rd | Data_Processing_1_rd | Load_Store_1_rd;  // OR_Gate or_5, 3 bits wide

  // Notes on the sheet:
  //   Extract carry
  //   Extract Opcode
  //   IF Reg_Imm=1 THEN use shift value from register ELSE use shift value from Imm5
  //   Buffer flags for next instruction
  //   Add 3 to offset because ARM pre-increments PC
  //   and does an additionnal prefect operation
endmodule

module Conditional (
  input  Enable,
  input  [15:0] Instruction,
  input  N,
  input  Z,
  input  C,
  input  V,
  output [7:0] Offset,
  output Verified
);
endmodule

module Opcode_Decoder (
  input  [5:0] Opcode,
  output Data_Processing,
  output SP_Address,
  output Load_Store,
  output Conditional,
  output Shift
);

  wire nb0, nb1, nb2, nb3, nb4, nb5;

  not not_1 (nb0, Opcode[0]);
  not not_2 (nb1, Opcode[1]);
  not not_3 (nb2, Opcode[2]);
  not not_4 (nb3, Opcode[3]);
  not not_5 (nb4, Opcode[4]);
  not not_6 (nb5, Opcode[5]);
  and and_1 (Data_Processing, nb5, Opcode[4], nb3, nb2, nb1, nb0);
  and and_2 (SP_Address, Opcode[5], nb4, Opcode[3], nb2, Opcode[1]);
  and and_3 (Load_Store, nb5, Opcode[4], nb3, Opcode[2]);
  and and_4 (Conditional, Opcode[5], Opcode[4], nb3, Opcode[2]);
  and and_5 (Shift, nb5, nb4);

  // Other names for the same wires on the sheet: b0 = Opcode[0]; b1 = Opcode[1]; b2 = Opcode[2]; b3 = Opcode[3];
  //   b4 = Opcode[4]; b5 = Opcode[5]

  // Notes on the sheet:
  //   SP Address
  //   Load/Store
  //   Conditional branch
  //   Shift, add, sub, mov
  //   Data Processing
endmodule

module Data_Processing (
  input  [15:0] Instruction,
  input  Enable,
  output [2:0] Rn,
  output [2:0] Rd,
  output [2:0] Rm,
  output [3:0] ALU_Opcode,
  output [3:0] Flags_Update_Mask
);


  // Notes on the sheet:
  //   Note 2: RSB instruction has Rn as 1st operand.
  //   MUL instruction has Rn as 1st operand and Rdm as 2nd operand
  //   Pull output low on Enable = 0
  //   For simplification purposes, Rm is used for 1st operand both here and in the ALU.
  //   Note: instructions that does not save the result will still have the second operand as the destination register, the ALU will copy the second register to the destination register
endmodule

module Shift_Add_Sub_Mov (
  input  Enable,
  input  [15:0] Instruction,
  output [3:0] ALU_Opcode,
  output [3:0] Flags_Update_Mask,
  output Carry,
  output Imm32_Enable,
  output [2:0] Rm,
  output [2:0] Rn,
  output [2:0] Rd,
  output [4:0] Imm5,
  output [31:0] Imm32
);

  wire ADD, ADD_IMM3, ASR, LSL, LSR, MOV, not_1_out, not_2_out, not_3_out, not_4_out, not_5_out, not_6_out,
       not_7_out, not_8_out, not_9_out, not_10_out, not_11_out, not_12_out, not_13_out, not_14_out, oth, SUB,
       SUB_IMM3;

  not not_1 (not_1_out, Instruction[11]);
  not not_2 (not_2_out, Instruction[12]);
  not not_3 (not_3_out, Instruction[13]);
  not not_4 (not_4_out, Instruction[11]);
  not not_5 (not_5_out, Instruction[13]);
  not not_6 (not_6_out, Instruction[12]);
  not not_7 (not_7_out, Instruction[13]);
  and and_1 (LSL, not_1_out, not_2_out, not_3_out);
  and and_2 (LSR, not_4_out, Instruction[12], not_5_out);
  and and_3 (ASR, Instruction[11], not_6_out, not_7_out);
  not not_8 (not_8_out, Instruction[11]);
  not not_9 (not_9_out, Instruction[12]);
  not not_10 (not_10_out, Instruction[12]);
  not not_11 (not_11_out, Instruction[11]);
  not not_12 (not_12_out, Instruction[12]);
  and and_4 (ADD, not_8_out, not_9_out, oth);
  and and_5 (SUB, Instruction[11], not_10_out, oth);
  and and_6 (MOV, not_11_out, not_12_out, Instruction[13]);
  and and_7 (oth, Instruction[11], Instruction[12], not_13_out);
  not not_13 (not_13_out, Instruction[13]);
  not not_14 (not_14_out, Instruction[11]);
  and and_8 (ADD_IMM3, not_14_out, Instruction[12], oth);
  and and_9 (SUB_IMM3, Instruction[11], Instruction[12], oth);

  // Other names for the same wires on the sheet: En = Enable; i0 = Instruction[0]; Imm8[7:0] = Instruction[7:0];
  //   inst[15:0] = Instruction; Rd_t[2:0] = Instruction[2:0]; i1 = Instruction[1]; i2 = Instruction[2];
  //   i3 = Instruction[3]; Rn_t[2:0] = Instruction[5:3]; i4 = Instruction[4]; i5 = Instruction[5];
  //   i6 = Instruction[6]; Imm3[2:0] = Instruction[8:6]; Imm5_t[4:0] = Instruction[10:6];
  //   Rm_t[2:0] = Instruction[8:6]; i7 = Instruction[7]; op0 = Instruction[11]; op1 = Instruction[12];
  //   op2 = Instruction[13]; op3 = Instruction[14]; op4 = Instruction[15]; i8 = Instruction[8];
  //   Rdm[2:0] = Instruction[10:8]; i9 = Instruction[9]; i10 = Instruction[10]

  // Notes on the sheet:
  //   Pull output low on Enable = 0
  //   Note 3: Imm32_Enable forces the use of the immediate for Rm register
  //   Enable carry for SUB since it is reversed in ALU
  //   Note: ALU uses Rn register for shifts. Use Rn instead of Rm for shifts (immediate) here too
  //   Note 2: MOV uses RSB ALU opcode with Imm8 reversed so that it is copied to output register
  //   ALU will use Imm32 instead of Rm
endmodule

module Load_Store (
  input  [15:0] Instruction,
  input  Enable,
  input  [31:0] Stack_Pointer,
  input  Clk,
  input  Reset,
  output Store,
  output Load,
  output PC_Hold,
  output [2:0] Rm,
  output [2:0] Rd,
  output [31:0] RAM_Addr
);


  // Notes on the sheet:
  //   Delay load and hold PC for 1 cycle for the RAM to send out requested data 
endmodule

module SP_Address (
  input  Enable,
  input  [15:0] Instruction,
  input  [31:0] Stack_Pointer,
  output Write_Enable,
  output [31:0] New_Stack_Pointer
);


  // Notes on the sheet:
  //   Pull output low on Enable = 0
endmodule

module Flags_APSR (
  input  [3:0] Flags_In,
  input  [3:0] Update_Mask,
  input  Clk,
  input  Rst,
  output [3:0] Flags_Out
);
endmodule
